# Fritzing sketch version2 (saved by Fritzing 0.9.3b)
circuit board: 10.9805cm x 6.12367cm
breadboards: 1

parts:
  Part1 = Arduino Uno (Rev3)
  R7 = Resistor [tolerance=±5% resistance=470 package=THT]
  R8 = Resistor [tolerance=±5% resistance=470 package=THT]
  R9 = Resistor [tolerance=±5% resistance=470 package=THT]
  LED1 = RGB LED (com. cathode, rgb) [package="5 mm [THT]"]
  LED2 = RGB LED (com. cathode, rgb) [package="5 mm [THT]"]
  LED3 = RGB LED (com. cathode, rgb) [package="5 mm [THT]"]
  R10 = Resistor [tolerance=±5% resistance=470 package=THT]
  LED4 = RGB LED (com. cathode, rgb) [package="5 mm [THT]"]
  LED5 = RGB LED (com. cathode, rgb) [package="5 mm [THT]"]
  LED6 = RGB LED (com. cathode, rgb) [package="5 mm [THT]"]
  R11 = Resistor [tolerance=±5% resistance=470 package=THT]
  LED7 = RGB LED (com. cathode, rgb) [package="5 mm [THT]"]
  LED8 = RGB LED (com. cathode, rgb) [package="5 mm [THT]"]
  LED9 = RGB LED (com. cathode, rgb) [package="5 mm [THT]"]
  R12 = Resistor [tolerance=±5% resistance=470 package=THT]
  R13 = Resistor [tolerance=±5% resistance=470 package=THT]
  R14 = Resistor [tolerance=±5% resistance=470 package=THT]
  R15 = Resistor [tolerance=±5% resistance=470 package=THT]
  Q1 = PNP-Transistor [package="TO92 [THT]"]
  Q2 = PNP-Transistor [package="TO92 [THT]"]
  Q3 = PNP-Transistor [package="TO92 [THT]"]
  J2 = female pin header, 1 pin [form="♀ (female)"]
  S19 = Pushbutton [package="[THT]"]
  S20 = Pushbutton [package="[THT]"]
  S21 = Pushbutton [package="[THT]"]
  S22 = Pushbutton [package="[THT]"]
  S23 = Pushbutton [package="[THT]"]
  S24 = Pushbutton [package="[THT]"]
  S25 = Pushbutton [package="[THT]"]
  S26 = Pushbutton [package="[THT]"]
  S27 = Pushbutton [package="[THT]"]
  R42 = Resistor [tolerance=±5% resistance=4.7k package=THT]
  R43 = Resistor [tolerance=±5% resistance=4.7k package=THT]
  R44 = Resistor [tolerance=±5% resistance=4.7k package=THT]
  R45 = Resistor [tolerance=±5% resistance=2.2k package=THT]
  R46 = Resistor [tolerance=±5% resistance=2.2k package=THT]
  R47 = Resistor [tolerance=±5% resistance=10k package=THT]
  R48 = Resistor [tolerance=±5% resistance=100 package=THT]
  R49 = Resistor [tolerance=±5% resistance=2.2k package=THT]
  R50 = Resistor [tolerance=±5% resistance=10k package=THT]
  R51 = Resistor [tolerance=±5% resistance=10k package=THT]
  R52 = Resistor [tolerance=±5% resistance=100 package=THT]
  R53 = Resistor [tolerance=±5% resistance=100 package=THT]
  J3 = female pin header, 1 pin [form="♀ (female)"]
  J4 = female pin header, 3 pins [form="♀ (female)"]
  J5 = female pin header, 2 pins [form="♀ (female)"]

nets:
  N1: Part1.A0, J4.pin1
  N2: Part1.A1, J4.pin2
  N3: Part1.A2, J4.pin3
  N4: Part1.A3, S19.Pin_1, S19.Pin_2, S20.Pin_1, S20.Pin_2, S21.Pin_1, S21.Pin_2, R42.Pin_1
  N5: Part1.A4/SDA, S22.Pin_1, S22.Pin_2, S23.Pin_1, S23.Pin_2, S26.Pin_1, S26.Pin_2, R43.Pin_1
  N6: Part1.A5/SCL, S24.Pin_1, S24.Pin_2, S25.Pin_1, S25.Pin_2, S27.Pin_1, S27.Pin_2, R44.Pin_1
  N7: Part1.D8, R8.Pin_0
  N8: Part1.D9_PWM, R9.Pin_0
  N9: Part1.D10_PWM/SS, Q2.B
  N10: Part1.D11_PWM/MOSI, Q1.B
  N11: Part1.D12/MISO, R7.Pin_0
  N12: Part1.D13/SCK, J2.pin1
  GND: Part1.GND, R45.Pin_0, R46.Pin_0, R47.Pin_1, R48.Pin_0, R49.Pin_0, R50.Pin_1, R51.Pin_1, R52.Pin_0, R53.Pin_0, J5.pin2
  N13: Part1.D2, R15.Pin_0
  N14: Part1.D3_PWM, R13.Pin_0
  N15: Part1.D4, R11.Pin_0
  N16: Part1.D5_PWM, R14.Pin_0
  N17: Part1.D6_PWM, R12.Pin_0
  N18: Part1.D7, R10.Pin_0
  5V: Part1.5V, Q1.C, Q2.C, Q3.C, R42.Pin_0, R43.Pin_0, R44.Pin_0, J5.pin1
  N19: R7.Pin_1, LED3.common_cathode
  N20: R8.Pin_1, LED1.common_cathode
  N21: R9.Pin_1, LED2.common_cathode
  N22: LED1.red_anode, LED2.red_anode, LED3.red_anode, LED4.red_anode, LED5.red_anode, LED6.red_anode, LED7.red_anode, LED8.red_anode, LED9.red_anode, Q3.E
  N23: LED1.green_anode, LED2.green_anode, LED3.green_anode, LED4.green_anode, LED5.green_anode, LED6.green_anode, Q2.E
  N24: LED1.blue_anode, LED2.blue_anode, LED3.blue_anode, LED4.blue_anode, LED5.blue_anode, LED6.blue_anode, LED7.blue_anode, LED8.blue_anode, LED9.blue_anode, Q1.E
  N25: R10.Pin_1, LED5.common_cathode
  N26: LED4.common_cathode, R14.Pin_1
  N27: LED6.common_cathode, R12.Pin_1
  N28: R11.Pin_1, LED8.common_cathode
  N29: LED7.common_cathode, R15.Pin_1
  N30: LED7.green_anode, LED8.green_anode, LED9.green_anode
  N31: LED9.common_cathode, R13.Pin_1
  N32: Q3.B, J3.pin1
  N33: S19.Pin_3, S19.Pin_4, R47.Pin_0
  N34: S20.Pin_3, S20.Pin_4, R52.Pin_1
  N35: S21.Pin_3, S21.Pin_4, R45.Pin_1
  N36: S22.Pin_4, R53.Pin_1
  N37: S23.Pin_4, R50.Pin_0
  N38: S24.Pin_3, S24.Pin_4, R48.Pin_1
  N39: S25.Pin_3, S25.Pin_4, R51.Pin_0
  N40: S26.Pin_3, S26.Pin_4, R49.Pin_1
  N41: S27.Pin_3, S27.Pin_4, R46.Pin_1

notes:
  E15 - B11
